# Fritzing sketch mandjgsm (saved by Fritzing 0.9.3b)
circuit board: 5.38307cm x 4.47152cm
stripboards: 1

parts:
  U1 = atmega328 [package=dip]
  J2 = Screw terminal - 2 pins [package=THT]
  J1 = female pin header, 7 pins [form="♀ (female)"]
  J3 = female pin header, 5 pins [form="♀ (female)"]
  S1 = Pushbutton [package="[THT]"]
  R1 = Resistor [tolerance=±5% resistance=10k package=THT]
  J4 = Screw terminal - 2 pins [package=THT]
  LED1 = LED - 3mm [color="Red (633nm)" package="3 mm [THT]"]
  C1 = Ceramic Capacitor [capacitance=100nF package="100 mil [THT, multilayer]"]
  J5 = Screw terminal - 2 pins [package=THT]
  R2 = Resistor [tolerance=±5% resistance=10k package=THT]
  R3 = Resistor [tolerance=±5% resistance=10k package=THT]
  R4 = Resistor [tolerance=±5% resistance=220 package=THT]
  LED2 = LED - 3mm [color="Green (560nm)" package="3 mm [THT]"]
  XTAL1 = Crystal [frequency="16 Mhz" package=THT]
  C2 = Ceramic Capacitor [capacitance=22pF package="100 mil [THT, multilayer]"]
  C3 = Ceramic Capacitor [capacitance=22pF package="100 mil [THT, multilayer]"]
  R5 = Resistor [tolerance=±5% resistance=220 package=THT]

nets:
  N1: U1.RESET, S1.Pin_3, S1.Pin_4, R1.Pin_1, C1.1
  N2: U1.D0_(RX), J3.pin3
  N3: U1.D1_(TX), J3.pin4
  N4: U1.D2, J1.pin3
  N5: U1.D3_(PWM), J1.pin4
  N6: U1.VCC, U1.AVCC, U1.AREF, J3.pin2, R1.Pin_0, J4.pin2, R2.Pin_0, R3.Pin_0, R5.Pin_1
  N7: U1.GND, J1.pin2, J3.pin1, S1.Pin_1, S1.Pin_2, J4.pin1, LED1.cathode, LED2.cathode, C2.0, C3.0
  N8: U1.XLAT1, XTAL1.pin_0, C2.1
  N9: U1.XLAT2, XTAL1.pin_1, C3.1
  N10: U1.D13, R4.Pin_1
  N11: U1.A4, J5.pin1, R3.Pin_1
  N12: U1.A5, J5.pin2, R2.Pin_1
  N13: J2.pin1, J1.pin6
  N14: J2.pin2, J1.pin7
  N15: J3.pin5, C1.0
  N16: LED1.anode, R5.Pin_0
  N17: R4.Pin_0, LED2.anode

notes:
  Rst Gnd SimRX SimTX VDD Gnd 5V
  Gnd 5v Tx Rx Dt
  M&J GSM
